# Fritzing sketch AbshirMohamud_PressureSensorV1 (saved by Fritzing 0.9.3b)
circuit board: 5.70415cm x 3.49423cm
breadboards: 1

parts:
  J1 = Basic Force Sensing Resistor (FSR) [package=THT]
  U1 = NodeMCU V1.0
  R1 = Resistor [tolerance=±5% resistance=10k package=THT]

nets:
  N1: J1.pin_0, U1.D1, R1.Pin_1
  N2: J1.pin_1, U1.3V3
  N3: U1.GND, R1.Pin_0

notes:
  Abshir M

custom parts:
  NodeMCU V1.0: ESP8266 based NodeMCU
