# Fritzing sketch PressureSensorPCB_AbshirMohamud (saved by Fritzing 0.9.3b)
circuit board: 6.46769cm x 5.7164cm
breadboards: 1

parts:
  Part1 = Arduino Uno (Rev3) - ICSP
  U2 = ESP8266 WiFi Module [part_number=ESP8266]
  J1 = Basic Force Sensing Resistor (FSR) [package=THT]
  R1 = Resistor [tolerance=±5% resistance=10k package=THT]

nets:
  N1: Part1.A0, J1.pin_1, R1.Pin_0
  GND: Part1.GND, U2.GND, R1.Pin_1
  N2: Part1.D0/RX, U2.RX
  N3: Part1.D1/TX, U2.TX
  3V3: Part1.3V3, U2.3.3V
  N4: Part1.5V, J1.pin_0
